# Fritzing sketch DIGITAL ELECTRONICS (saved by Fritzing 0.9.3b)
breadboards: 2

parts:
  SPEAKER = Piezo Speaker
  R2 = Resistor [tolerance=±5% resistance=72k package=THT]
  PULSER = 555 Timer [package="DIP8 [THT]"]
  C7 = Electrolytic Capacitor [capacitance=10µF package="100 mil [THT, electrolytic]"]
  COUNTER = IC, DIP package, 14 pins [chip_label=74L93]
  7_SEG_DECODER = IC, DIP package, 16 pins [chip_label=74LS48]
  DISPLAY = 7 Segment Display
  R1 = Resistor [tolerance=±5% resistance=100 package=THT]
  4_BIT_COMPARATOR = DIP - 16 pins [chip_label=M74HC85 package="DIP (Dual Inline) [THT]"]
  C9 = Ceramic Capacitor [capacitance=10nF package="100 mil [THT, multilayer]"]
  R11 = Resistor [tolerance=±5% resistance=100 package=THT]
  INDICATOR = LED - 5mm [color="Green (570nm)" package="5 mm [THT]"]
  BAT2 = LIPO-110mAh [package=lipo-110]

nets:
  GND: SPEAKER.pin1, PULSER.Ground, C7.-, COUNTER.pin10, 7_SEG_DECODER.pin8, DISPLAY.common_cathode, 4_BIT_COMPARATOR.GND, 4_BIT_COMPARATOR.B1, 4_BIT_COMPARATOR.B2, C9.0, INDICATOR.cathode, BAT2.-
  N1: SPEAKER.pin2, 4_BIT_COMPARATOR.A=B_out
  N2: R2.Pin_0, PULSER.Trigger, PULSER.Threshold, C7.+
  N3: R2.Pin_1, PULSER.Discharge, R1.Pin_1
  N4: PULSER.Output, COUNTER.pin1, R11.Pin_0
  N5: PULSER.Reset, PULSER.Vcc_Supply_Voltage, COUNTER.pin5, 7_SEG_DECODER.pin16, R1.Pin_0, 4_BIT_COMPARATOR.B3, 4_BIT_COMPARATOR.B0, 4_BIT_COMPARATOR.Vcc, BAT2.+
  N6: PULSER.Control_Voltage, C9.1
  N7: COUNTER.pin2, COUNTER.pin11, 7_SEG_DECODER.pin6, 4_BIT_COMPARATOR.A3
  N8: COUNTER.pin3, COUNTER.pin9, 7_SEG_DECODER.pin1, 4_BIT_COMPARATOR.A1
  N9: COUNTER.pin8, 7_SEG_DECODER.pin2, 4_BIT_COMPARATOR.A2
  N10: COUNTER.pin12, COUNTER.pin14, 7_SEG_DECODER.pin7, 4_BIT_COMPARATOR.A0
  N11: 7_SEG_DECODER.pin9, DISPLAY.Segment_E
  N12: 7_SEG_DECODER.pin10, DISPLAY.Segment_D
  N13: 7_SEG_DECODER.pin11, DISPLAY.Segment_C
  N14: 7_SEG_DECODER.pin12, DISPLAY.Segment_B
  N15: 7_SEG_DECODER.pin13, DISPLAY.Segment_A
  N16: 7_SEG_DECODER.pin14, DISPLAY.Segment_G
  N17: 7_SEG_DECODER.pin15, DISPLAY.Segment_F
  N18: R11.Pin_1, INDICATOR.anode

custom parts:
  7 Segment Display: 7 Segment Display with common cathode.
  DIP - 16 pins: A DIP stand-in part for whatever IC you want. With 16 pins on a 300mil dual inline package (DIP) footprint.
