# Fritzing sketch Decodificador 7447 (saved by Fritzing 0.9.3b)
circuit board: 8.46667cm x 5.64444cm
breadboards: 1

parts:
  Parte1 = Arduino Uno (Rev3)
  U2 = SN74LS47N [package="DIP16 [THT]"]
  DI1-U = 7-Segment LED Display [package=THT]
  DI2-D = 7-Segment LED Display [package=THT]
  R2 = Resistor [tolerance=±5% resistance=330 package=THT]
  R1 = Resistor [tolerance=±5% resistance=330 package=THT]
  U1 = SN74LS47N [package="DIP16 [THT]"]

nets:
  N1: Parte1.D8, U1.C
  N2: Parte1.D9_PWM, U1.D
  N3: Parte1.D10_PWM/SS, U2.A
  N4: Parte1.D11_PWM/MOSI, U2.B
  N5: Parte1.D12/MISO, U2.C
  N6: Parte1.D13/SCK, U2.D
  GND: Parte1.GND, U2.GND, U1.GND
  N7: Parte1.D6_PWM, U1.A
  N8: Parte1.D7, U1.B
  VCC: Parte1.5V, U2.VCC, R2.Pin_0, R1.Pin_0, U1.VCC
  N9: U2.e, DI2-D.cathodeE
  N10: U2.d, DI2-D.cathodeD
  N11: U2.c, DI2-D.cathodeC
  N12: U2.b, DI2-D.cathodeB
  N13: U2.a, DI2-D.cathodeA
  N14: U2.g, DI2-D.cathodeG
  N15: U2.f, DI2-D.cathodeF
  N16: DI1-U.cathodeE, U1.e
  N17: DI1-U.cathodeD, U1.d
  N18: DI1-U.cathodeC, U1.c
  N19: DI1-U.cathodeB, U1.b
  N20: DI1-U.cathodeA, U1.a
  N21: DI1-U.commAnode#7, R1.Pin_1
  N22: DI1-U.cathodeF, U1.f
  N23: DI1-U.cathodeG, U1.g
  N24: DI2-D.commAnode#7, R2.Pin_1

custom parts:
  SN74LS47N: BCD-TO-SEVEN-SEGMENT DECODERS/DRIVRES

// code stored in the sketch: Decodificador 7447.ino
// Ing. Andrés Orozco Escobar
// aorozco@comfamiliar.edu.co
// COMFAMILIAR RISARALDA
// Semillero Hardware Libre
// Contador 00 a 99 con Decodificador BCD a 7-Segment 7447
// @Mayo 2015

const char PinAU = 9; // Pines asignados a la unidad, orden 7447 (B=6 Pin 1, C=7 Pin 2, D=8 Pin 6, A=9 Pin 7)
const char PinBU = 6;
const char PinCU = 7;
const char PinDU = 8;

const char PinAD = 13; // Pines asignados a la decena, orden 7447 (B=10 Pin 1, C=11 Pin 2, D= Pin 12, A=9 Pin 13)
const char PinBD = 10;
const char PinCD = 11;
const char PinDD = 12;


void setup(){
pinMode(PinAU, OUTPUT);
pinMode(PinBU, OUTPUT);
pinMode(PinCU, OUTPUT);
pinMode(PinDU, OUTPUT);
pinMode(PinAD, OUTPUT);
pinMode(PinBD, OUTPUT);
pinMode(PinCD, OUTPUT);
pinMode(PinDD, OUTPUT);
}


void loop(){
  // Contador 00-99
  char i = 0, j = 0;
      for (; j < 10; j++){
      for (; i < 10; i++){
      numero(j,i); // Decena, Unidad
      delay (200);
      }
      i=0;
      }
  // Contador 99-00
/*  char i = 9, j = 9;
      for (; j >= 0; j--){
      for (; i >= 0; i--){
      numero(j,i); // Decena, Unidad
      delay (200);
      }
      i=9;
      }
  // Numero especifico
numero(2,2);*/
}


void U(char D, char C, char B, char A){ // Orden Binario DCBA
digitalWrite(PinAU,A);
digitalWrite(PinBU,B);
digitalWrite(PinCU,C);
digitalWrite(PinDU,D);
}


void D(char D, char C, char B, char A){ // Orden Binario DCBA
digitalWrite(PinAD,A);
digitalWrite(PinBD,B);
digitalWrite(PinCD,C);
digitalWrite(PinDD,D);
}


void numero (char decena, char unidad){
switch (unidad) {
    case 0: // Número 0 en la Unidad
      U(0,0,0,0);
    break;
    case 1: // Número 1 en la Unidad
      U(0,0,0,1);
    break;
    case 2: // Número 2 en la Unidad
      U(0,0,1,0);
    break;
    case 3: // Número 3 en la Unidad
      U(0,0,1,1);
    break;
    case 4: // Número 4 en la Unidad
      U(0,1,0,0);
    break;
    case 5: // Número 5 en la Unidad
      U(0,1,0,1);
    break;
    case 6: // Número 6 en la Unidad
      U(0,1,1,0);
    break;
    case 7: // Número 7 en la Unidad
      U(0,1,1,1);
    break;    
    case 8: // Número 8 en la Unidad
      U(1,0,0,0);
    break;
    case 9: // Número 9 en la Unidad
      U(1,0,0,1);
    break;    
    }
switch (decena) {
    case 0: // Número 0 en la Decena
      D(0,0,0,0);
    break;
    case 1: // Número 1 en la Decena
      D(0,0,0,1);
    break;
    case 2: // Número 2 en la Decena
      D(0,0,1,0);
    break;
    case 3: // Número 3 en la Decena
      D(0,0,1,1);
    break;
    case 4: // Número 4 en la Decena
      D(0,1,0,0);
    break;
    case 5: // Número 5 en la Decena
      D(0,1,0,1);
    break;
    case 6: // Número 6 en la Decena
      D(0,1,1,0);
    break;
    case 7: // Número 7 en la Decena
      D(0,1,1,1);
    break;    
    case 8: // Número 8 en la Decena
      D(1,0,0,0);
    break;
    case 9: // Número 9 en la Decena
      D(1,0,0,1);
    break;    
    }    
}
