# Fritzing sketch LED-C-R (saved by Fritzing 0.9.3b)
breadboards: 1

parts:
  S1 = Pushbutton [package="[SMD]"]
  R1 = Resistor [tolerance=±5% resistance=220 package=THT]
  LED1 = LED - 5mm [color="Red (633nm)" package="5 mm [THT]"]
  C1 = Electrolytic Capacitor [capacitance=1µF package="100 mil [THT, electrolytic]"]
  VCC1 = Battery

nets:
  N1: S1.Pin_1, S1.Pin_2, R1.Pin_0, C1.+, VCC1.+
  N2: S1.Pin_3, S1.Pin_4
  N3: R1.Pin_1, LED1.anode
  N4: LED1.cathode, C1.-, VCC1.-
