# Fritzing sketch OKQWODKMKAWDM (saved by Fritzing 0.9.3b)
breadboards: 1

parts:
  IC1 = IC, DIP package, 14 pins [chip_label=IC]

nets:
  N1: IC1.pin1, IC1.pin14
  N2: IC1.pin2, IC1.pin13
  N3: IC1.pin3, IC1.pin12
  N4: IC1.pin4, IC1.pin11
  N5: IC1.pin5, IC1.pin10
  N6: IC1.pin6, IC1.pin9
  N7: IC1.pin7, IC1.pin8
