# Fritzing sketch dice 7493 (saved by Fritzing 0.9.3b)
breadboards: 1

parts:
  IC1 = IC, DIP package, 14 pins [chip_label=74LS93]
  IC2 = IC, DIP package, 14 pins [chip_label=74LS04]
  R1 = Resistor [tolerance=±5% resistance=220 package=THT]
  C1 = Electrolytic Capacitor [capacitance=1µF package="100 mil [THT, electrolytic]"]
  S1 = Pushbutton [package="[THT]"]
  R2 = Resistor [tolerance=±5% resistance=220 package=THT]
  LED1 = LED - 5mm [color="Red (633nm)" package="5 mm [THT]"]
  R3 = Resistor [tolerance=±5% resistance=220 package=THT]
  LED2 = LED - 5mm [color="Red (633nm)" package="5 mm [THT]"]
  LED3 = LED - 5mm [color="Red (633nm)" package="5 mm [THT]"]
  R4 = Resistor [tolerance=±5% resistance=220 package=THT]
  R5 = Resistor [tolerance=±5% resistance=220 package=THT]

nets:
  N1: IC1.pin1, S1.Pin_1, S1.Pin_2, R2.Pin_1
  N2: IC1.pin2, IC1.pin11, LED1.anode
  N3: IC1.pin3, IC1.pin8, LED2.anode
  N4: IC1.pin9, LED3.anode
  N5: IC1.pin14, IC2.pin14
  N6: IC2.pin1, R1.Pin_1, C1.+
  N7: IC2.pin2, IC2.pin3, R1.Pin_0
  N8: IC2.pin4, IC2.pin5, C1.-
  N9: IC2.pin6, S1.Pin_3, S1.Pin_4
  N10: IC2.pin7, R2.Pin_0, R3.Pin_0, R4.Pin_0, R5.Pin_0
  N11: LED1.cathode, R3.Pin_1
  N12: LED2.cathode, R4.Pin_1
  N13: LED3.cathode, R5.Pin_1
