# Fritzing sketch digital clock (saved by Fritzing 0.9.3b)
breadboards: 2

parts:
  COUNTER = IC, DIP package, 14 pins [chip_label=74L93]
  7_SEG_DECODER = IC, DIP package, 16 pins [chip_label=74LS48]
  R5 = Resistor [tolerance=±5% resistance=72 package=THT]
  C5 = Electrolytic Capacitor [capacitance=10µF package="100 mil [THT, electrolytic]"]
  PULSER1 = 555 Timer [package="DIP8 [THT]"]
  DISPLAY = 7 Segment Display
  R6 = Resistor [tolerance=±5% resistance=100 package=THT]
  C6 = Ceramic Capacitor [capacitance=10nF package="100 mil [THT, multilayer]"]
  PULSE_INDICATOR = LEDs [package=led10mm]
  R7 = Resistor [tolerance=±5% resistance=100 package=THT]
  J1 = Piezo Speaker
  BAT1 = LIPO-110mAh [package=lipo-110]
  4_BIT_COMPARATOR = IC, DIP package, 16 pins [chip_label=M74HC85]
  IC1 = DIP - 16 pins [chip_label=M74HC85 package="DIP (Dual Inline) [THT]"]  # not connected
  IC2 = DIP - 16 pins [chip_label=M74HC85 package="DIP (Dual Inline) [THT]"]  # not connected

nets:
  N1: COUNTER.pin1, PULSER1.Output, R7.Pin_0
  N2: COUNTER.pin2, COUNTER.pin11, 7_SEG_DECODER.pin6, 4_BIT_COMPARATOR.pin15
  N3: COUNTER.pin3, COUNTER.pin9, 7_SEG_DECODER.pin1, 4_BIT_COMPARATOR.pin12
  N4: COUNTER.pin5, 7_SEG_DECODER.pin16, PULSER1.Reset, PULSER1.Vcc_Supply_Voltage, R6.Pin_0, BAT1.+, 4_BIT_COMPARATOR.pin1, 4_BIT_COMPARATOR.pin9, 4_BIT_COMPARATOR.pin16
  N5: COUNTER.pin8, 7_SEG_DECODER.pin2, 4_BIT_COMPARATOR.pin13
  GND: COUNTER.pin10, 7_SEG_DECODER.pin8, C5.-, PULSER1.Ground, DISPLAY.common_cathode, C6.0, PULSE_INDICATOR.C, J1.pin2, BAT1.-, 4_BIT_COMPARATOR.pin8, 4_BIT_COMPARATOR.pin11, 4_BIT_COMPARATOR.pin14
  N6: COUNTER.pin12, COUNTER.pin14, 7_SEG_DECODER.pin7, 4_BIT_COMPARATOR.pin10
  N7: 7_SEG_DECODER.pin9, DISPLAY.Segment_E
  N8: 7_SEG_DECODER.pin10, DISPLAY.Segment_D
  N9: 7_SEG_DECODER.pin11, DISPLAY.Segment_C
  N10: 7_SEG_DECODER.pin12, DISPLAY.Segment_B
  N11: 7_SEG_DECODER.pin13, DISPLAY.Segment_A
  N12: 7_SEG_DECODER.pin14, DISPLAY.Segment_G
  N13: 7_SEG_DECODER.pin15, DISPLAY.Segment_F
  N14: R5.Pin_0, C5.+, PULSER1.Trigger, PULSER1.Threshold
  N15: R5.Pin_1, PULSER1.Discharge, R6.Pin_1
  N16: PULSER1.Control_Voltage, C6.1
  N17: PULSE_INDICATOR.A, R7.Pin_1
  N18: J1.pin1, 4_BIT_COMPARATOR.pin6

custom parts:
  7 Segment Display: 7 Segment Display with common cathode.
  DIP - 16 pins: A DIP stand-in part for whatever IC you want. With 16 pins on a 300mil dual inline package (DIP) footprint.
  DIP - 16 pins: A DIP stand-in part for whatever IC you want. With 16 pins on a 300mil dual inline package (DIP) footprint.
