# Fritzing sketch timerBarometer (saved by Fritzing 0.9.3b)
breadboards: 1

parts:
  Nano1 = Arduino Nano v2.3
  LCD1 = LCD screen
  Часть2 = Real Time Clock Module - DS1307 RTC Breakout Board
  C1 = Electrolytic Capacitor [capacitance=47µF voltage=6.3V package="100 mil [THT, electrolytic]"]
  Часть3 = Barometric Pressure Sensor - BMP085 Breakout
  part = Arduino Nano v2.3  # not connected

nets:
  GND: Nano1.GND, LCD1.VSS, LCD1.R/W, LCD1.LED-, Часть2.GND, C1.-, Часть3.GND
  N1: Nano1.D2, LCD1.DB7
  N2: Nano1.D3, LCD1.DB6
  N3: Nano1.D4, LCD1.DB5
  N4: Nano1.D5, LCD1.DB4
  N5: Nano1.D10, LCD1.V0, C1.+
  N6: Nano1.D11, LCD1.E
  N7: Nano1.D12, LCD1.RS
  3V3: Nano1.3V3, Часть3.VCC
  N8: Nano1.A5, Часть2.SCL, Часть3.SCL
  N9: Nano1.A4, Часть2.SDA, Часть3.SDA
  +5V: Nano1.+5V, LCD1.VDD, LCD1.LED+, Часть2.5V

notes:
  Green (SDA) & Orange (SCL) wires are I²C bus
  Black wires are GND
  Brown wire is 3.3V
  Red wires are 5V
  BMP085 3.3v Sensor
