# Fritzing sketch workshop resistrors (saved by Fritzing 0.9.3b)
stripboards: 1

parts:
  R2 = Resistor [tolerance=±5% resistance=750 package=THT]
  R3 = Resistor [tolerance=±5% resistance=4.7k package=THT]
  R4 = Resistor [tolerance=±5% resistance=68k package=THT]
  J2 = female pin header, 1 pin [form="♀ (female)"]
  J3 = female pin header, 1 pin [form="♀ (female)"]
  J4 = female pin header, 1 pin [form="♀ (female)"]
  J5 = female pin header, 1 pin [form="♀ (female)"]
  R1 = Resistor [tolerance=±5% resistance=750 package=THT]

nets:
  N1: R2.Pin_0, R4.Pin_0, J2.pin1, R1.Pin_1
  N2: R2.Pin_1, R3.Pin_1, R4.Pin_1, J3.pin1
  N3: R3.Pin_0, J4.pin1
  N4: J5.pin1, R1.Pin_0
